// Logisim project Logisim projeto.circ as structural Verilog: 14 circuits, main circuit main
module main (
  input  in_1,
  input  in_2,
  input  in_3,
  input  in_4,
  input  in_5,
  input  in_6,
  input  in_7,
  input  in_8,
  input  Jogar,
  input  Jogador,
  output Maior,
  output Igual,
  output Menor
);

  wire led_1_out_5, led_1_out_6, led_1_out_7, led_1_out_8, led_1_out_9, led_1_out_10, led_1_out_11,
       led_2_out_5, led_2_out_6, led_2_out_7, led_2_out_8, led_2_out_9, led_2_out_10, led_2_out_11;

  _7_Segment_Display u_7_segment_display_1 (
    .g(led_1_out_11), .f(led_1_out_10), .a(led_1_out_5), .b(led_1_out_6), .e(led_1_out_9), .d(led_1_out_8),
    .c(led_1_out_7));  // open: dp
  LED led_1 (
    .out_5(led_1_out_5), .out_6(led_1_out_6), .out_7(led_1_out_7), .out_8(led_1_out_8), .out_9(led_1_out_9),
    .out_10(led_1_out_10), .out_11(led_1_out_11), .X(in_4), .Y(in_3), .Z(in_2), .W(in_1));
  LED led_2 (
    .out_5(led_2_out_5), .out_6(led_2_out_6), .out_7(led_2_out_7), .out_8(led_2_out_8), .out_9(led_2_out_9),
    .out_10(led_2_out_10), .out_11(led_2_out_11), .X(in_8), .Y(in_7), .Z(in_6), .W(in_5));
  _7_Segment_Display u_7_segment_display_2 (
    .g(led_2_out_11), .f(led_2_out_10), .a(led_2_out_5), .b(led_2_out_6), .e(led_2_out_9), .d(led_2_out_8),
    .c(led_2_out_7));  // open: dp
  Game game_1 (
    .Jogar(Jogar), .in_2({in_4, in_3, in_2, in_1}), .in_3({in_8, in_7, in_6, in_5}), .Jogador(Jogador),
    .Maior(Maior), .Igual(Igual), .Menor(Menor));

  // Notes on the sheet:
  //   Jogador 0
  //   Jogador 1
endmodule

module Game (
  input  Jogar,
  input  [3:0] in_2,
  input  [3:0] in_3,
  input  Jogador,
  output Maior,
  output Igual,
  output Menor
);

  wire comparador_4_bits_1_igual, comparador_4_bits_1_maior, comparador_4_bits_1_menor;
  wire [3:0] mux_1_out_4;

  Mux mux_1 (.A(in_2[0]), .B(in_3[0]), .C(Jogador), .out_4(mux_1_out_4[0]));
  Mux mux_2 (.A(in_2[1]), .B(in_3[1]), .C(Jogador), .out_4(mux_1_out_4[1]));
  Mux mux_3 (.A(in_2[2]), .B(in_3[2]), .C(Jogador), .out_4(mux_1_out_4[2]));
  Mux mux_4 (.A(in_2[3]), .B(in_3[3]), .C(Jogador), .out_4(mux_1_out_4[3]));
  Comparador_4_bits comparador_4_bits_1 (
    .in_1(mux_1_out_4), .in_2(4'b0110), .Maior(comparador_4_bits_1_maior), .Igual(comparador_4_bits_1_igual),
    .Menor(comparador_4_bits_1_menor));
  and and_1 (Maior, Jogar, comparador_4_bits_1_maior);
  and and_2 (Igual, Jogar, comparador_4_bits_1_igual);
  and and_3 (Menor, comparador_4_bits_1_menor, Jogar);
endmodule

module Mux (
  input  A,
  input  B,
  input  C,
  output out_4
);

  wire and_1_out, and_2_out, and_3_out, and_4_out;

  and and_1 (and_1_out, ~A, B, C);  // AND_Gate
  and and_2 (and_2_out, A, ~B, ~C);  // AND_Gate
  and and_3 (and_3_out, A, B, ~C);  // AND_Gate
  and and_4 (and_4_out, A, B, C);
  or or_1 (out_4, and_1_out, and_2_out, and_3_out, and_4_out);
endmodule

module Comparador_1_bit (
  input  in_1,
  input  in_2,
  output Maior,
  output Igual,
  output Menor
);

  and and_1 (Menor, in_2, ~in_1);  // AND_Gate
  xnor xnor_1 (Igual, in_1, in_2);
  and and_2 (Maior, ~in_2, in_1);  // AND_Gate
endmodule

module comparador_Recursivo (
  input  in_1,
  input  in_2,
  input  in_3,
  input  in_4,
  input  in_5,
  output Maior,
  output Igual,
  output Menor
);

  wire and_2_out, and_3_out, comparador_1_bit_1_igual, comparador_1_bit_1_maior, comparador_1_bit_1_menor;

  Comparador_1_bit comparador_1_bit_1 (
    .in_1(in_2), .in_2(in_3), .Maior(comparador_1_bit_1_maior), .Igual(comparador_1_bit_1_igual),
    .Menor(comparador_1_bit_1_menor));
  and and_1 (Igual, in_1, comparador_1_bit_1_igual);
  and and_2 (and_2_out, in_1, comparador_1_bit_1_maior);
  and and_3 (and_3_out, comparador_1_bit_1_menor, in_1);
  or or_1 (Maior, and_2_out, in_4);
  or or_2 (Menor, and_3_out, in_5);
endmodule

module A (
  input  W,
  input  Z,
  input  Y,
  input  X,
  output out_5
);

  wire and_1_out, and_2_out, and_3_out, and_4_out, and_5_out, and_6_out, and_7_out, not_1_out, not_2_out,
       not_3_out, not_4_out, not_5_out, not_6_out, not_7_out, not_8_out, not_9_out, not_10_out;

  not not_1 (not_1_out, X);
  not not_2 (not_2_out, X);
  not not_3 (not_3_out, Y);
  not not_4 (not_4_out, Z);
  not not_5 (not_5_out, X);
  not not_6 (not_6_out, Z);
  not not_7 (not_7_out, W);
  not not_8 (not_8_out, W);
  not not_9 (not_9_out, Y);
  not not_10 (not_10_out, Z);
  and and_1 (and_1_out, not_2_out, not_3_out, not_4_out);
  and and_2 (and_2_out, not_5_out, Z, W);
  and and_3 (and_3_out, Y, not_6_out, not_7_out);
  and and_4 (and_4_out, X, Y, Z);
  and and_5 (and_5_out, X, Z, not_8_out);
  and and_6 (and_6_out, not_9_out, W, not_10_out);
  and and_7 (and_7_out, not_1_out, Y);
  or or_1 (out_5, and_7_out, and_1_out, and_2_out, and_3_out, and_4_out, and_5_out, and_6_out);
endmodule

module B (
  input  W,
  input  Z,
  input  Y,
  input  X,
  output out_5
);

  wire and_1_out, and_2_out, and_3_out, and_4_out, and_5_out, not_1_out, not_2_out, not_3_out, not_4_out,
       not_5_out, not_6_out, not_7_out, not_8_out, not_9_out;

  not not_1 (not_1_out, X);
  not not_2 (not_2_out, Z);
  not not_3 (not_3_out, X);
  not not_4 (not_4_out, Y);
  not not_5 (not_5_out, W);
  not not_6 (not_6_out, W);
  not not_7 (not_7_out, Y);
  not not_8 (not_8_out, Z);
  and and_1 (and_1_out, not_8_out, not_9_out);
  not not_9 (not_9_out, W);
  and and_2 (and_2_out, not_1_out, W, not_2_out);
  and and_3 (and_3_out, not_3_out, not_4_out, not_5_out);
  and and_4 (and_4_out, X, Y, not_6_out);
  and and_5 (and_5_out, X, not_7_out, W);
  or or_1 (out_5, and_1_out, and_2_out, and_3_out, and_4_out, and_5_out);
endmodule

module C (
  input  W,
  input  Z,
  input  Y,
  input  X,
  output out_5
);

  wire and_1_out, and_2_out, and_3_out, and_4_out, and_5_out, not_1_out, not_2_out, not_3_out, not_4_out,
       not_5_out, not_6_out, not_7_out;

  not not_1 (not_1_out, Z);
  not not_2 (not_2_out, W);
  not not_3 (not_3_out, Y);
  not not_4 (not_4_out, X);
  not not_5 (not_5_out, Y);
  not not_6 (not_6_out, Z);
  not not_7 (not_7_out, W);
  and and_1 (and_1_out, not_1_out, W);
  and and_2 (and_2_out, Z, not_2_out);
  and and_3 (and_3_out, X, not_3_out);
  and and_4 (and_4_out, not_4_out, not_4_out, not_5_out, not_6_out);
  and and_5 (and_5_out, X, Y, not_7_out);
  or or_1 (out_5, and_1_out, and_2_out, and_3_out, and_4_out, and_5_out);
endmodule

module D (
  input  W,
  input  Z,
  input  Y,
  input  X,
  output out_5
);

  wire and_1_out, and_2_out, and_3_out, and_4_out, and_5_out, and_6_out, not_1_out, not_2_out, not_3_out,
       not_4_out, not_5_out, not_6_out, not_7_out, not_8_out, not_9_out, not_10_out;

  not not_1 (not_1_out, X);
  and and_1 (and_1_out, not_1_out, not_2_out, not_3_out);
  not not_2 (not_2_out, Y);
  not not_3 (not_3_out, Z);
  not not_4 (not_4_out, X);
  and and_2 (and_2_out, not_4_out, Z, W);
  not not_5 (not_5_out, Z);
  and and_3 (and_3_out, Y, not_5_out, not_6_out);
  not not_6 (not_6_out, W);
  not not_7 (not_7_out, Z);
  and and_4 (and_4_out, X, not_7_out, W);
  and and_5 (and_5_out, X, not_8_out, Z);
  not not_8 (not_8_out, Y);
  not not_9 (not_9_out, X);
  and and_6 (and_6_out, not_9_out, Y, not_10_out);
  not not_10 (not_10_out, W);
  or or_1 (out_5, and_1_out, and_2_out, and_3_out, and_4_out, and_5_out, and_6_out);
endmodule

module E (
  input  W,
  input  Z,
  input  Y,
  input  X,
  output out_5
);

  wire and_1_out, and_2_out, and_3_out, and_4_out;

  and and_1 (and_1_out, ~X, Y);  // AND_Gate
  and and_2 (and_2_out, Z, W);
  and and_3 (and_3_out, ~X, ~Y, ~Z);  // AND_Gate
  and and_4 (and_4_out, X, Y, W);
  or or_1 (out_5, and_1_out, and_2_out, and_3_out, and_4_out);
endmodule

module F (
  input  W,
  input  Z,
  input  Y,
  input  X,
  output out_5
);

  wire and_1_out, and_2_out, and_3_out, and_4_out, and_5_out;

  and and_1 (and_1_out, ~X, ~Y);  // AND_Gate
  and and_2 (and_2_out, ~Z, W);  // AND_Gate
  and and_3 (and_3_out, ~Y, Z, ~W);  // AND_Gate
  and and_4 (and_4_out, ~X, Y, Z);  // AND_Gate
  and and_5 (and_5_out, X, Y, W);
  or or_1 (out_5, and_1_out, and_2_out, and_3_out, and_4_out, and_5_out);
endmodule

module G (
  input  W,
  input  Z,
  input  Y,
  input  X,
  output out_5
);

  wire and_1_out, and_2_out, and_3_out, and_4_out, and_5_out;

  and and_1 (and_1_out, X, ~Y);  // AND_Gate
  and and_2 (and_2_out, ~Z, W);  // AND_Gate
  and and_3 (and_3_out, X, Z, W);
  and and_4 (and_4_out, ~Y, Z, ~W);  // AND_Gate
  and and_5 (and_5_out, Y, ~Z, ~W);  // AND_Gate
  or or_1 (out_5, and_1_out, and_2_out, and_3_out, and_4_out, and_5_out);
endmodule

module LED (
  input  X,
  input  Y,
  input  Z,
  input  W,
  output out_5,
  output out_6,
  output out_7,
  output out_8,
  output out_9,
  output out_10,
  output out_11
);

  A a_1 (.W(W), .Z(Z), .Y(Y), .X(X), .out_5(out_5));
  B b_1 (.W(W), .Z(Z), .Y(Y), .X(X), .out_5(out_6));
  C c_1 (.W(W), .Z(Z), .Y(Y), .X(X), .out_5(out_7));
  D d_1 (.W(W), .Z(Z), .Y(Y), .X(X), .out_5(out_8));
  E e_1 (.W(W), .Z(Z), .Y(Y), .X(X), .out_5(out_9));
  F f_1 (.W(W), .Z(Z), .Y(Y), .X(X), .out_5(out_10));
  G g_1 (.W(W), .Z(Z), .Y(Y), .X(X), .out_5(out_11));
endmodule

// Comp
module Comparador_4_bits (
  input  [3:0] in_1,
  input  [3:0] in_2,
  output Maior,
  output Igual,
  output Menor
);

  wire comparador_1_bit_1_igual, comparador_1_bit_1_maior, comparador_1_bit_1_menor,
       comparador_recursivo_1_igual, comparador_recursivo_1_maior, comparador_recursivo_1_menor,
       comparador_recursivo_2_igual, comparador_recursivo_2_maior, comparador_recursivo_2_menor;

  Comparador_1_bit comparador_1_bit_1 (
    .in_1(in_1[3]), .in_2(in_2[3]), .Maior(comparador_1_bit_1_maior), .Igual(comparador_1_bit_1_igual),
    .Menor(comparador_1_bit_1_menor));
  comparador_Recursivo comparador_recursivo_1 (
    .in_1(comparador_1_bit_1_igual), .in_2(in_1[2]), .in_3(in_2[2]), .in_4(comparador_1_bit_1_maior),
    .in_5(comparador_1_bit_1_menor), .Maior(comparador_recursivo_1_maior),
    .Igual(comparador_recursivo_1_igual), .Menor(comparador_recursivo_1_menor));
  comparador_Recursivo comparador_recursivo_2 (
    .in_1(comparador_recursivo_1_igual), .in_2(in_1[1]), .in_3(in_2[1]), .in_4(comparador_recursivo_1_maior),
    .in_5(comparador_recursivo_1_menor), .Maior(comparador_recursivo_2_maior),
    .Igual(comparador_recursivo_2_igual), .Menor(comparador_recursivo_2_menor));
  comparador_Recursivo comparador_recursivo_3 (
    .in_1(comparador_recursivo_2_igual), .in_2(in_1[0]), .in_3(in_2[0]), .in_4(comparador_recursivo_2_maior),
    .in_5(comparador_recursivo_2_menor), .Maior(Maior), .Igual(Igual), .Menor(Menor));
endmodule
